// Logisim project Ansaripour-Darya_610300022-project.circ as structural Verilog: 31 circuits, main circuit main
module main (
  input  [7:0] INP,
  output [15:0] out_2,
  output [15:0] out_3,
  output [15:0] out_4,
  output [15:0] out_5,
  output [15:0] out_6,
  output [15:0] out_7,
  output [7:0] out_8,
  output out_9
);

  wire ac_ctrl_1_clr, ac_ctrl_1_inc, ALU_E, and_1_out, and_2_out, and_4_out, ar_ctrl_1_clr, ar_ctrl_1_inr,
       ar_ctrl_1_ld, bus_ctrl_1_s0, bus_ctrl_1_s1, bus_ctrl_1_s2, CLK, clock_1_out, dr_ctrl_1_inr,
       dr_ctrl_1_ld, e_ctrl_1_clr, e_ctrl_1_en, e_ctrl_1_j, e_ctrl_1_k, FGI, fgi_ctrl_1_j, fgi_ctrl_1_k, FGO,
       fgo_ctrl_1_j, fgo_ctrl_1_k, HLT, IEN, ien_ctrl_1_j, ien_ctrl_1_k, ir_ctrl_1_ld, not_1_out, or_1_out,
       or_2_out, or_3_out, outr_ctrl_1_ld, pc_ctrl_1_clr, pc_ctrl_1_inr, pc_ctrl_1_ld, R, r_ctrl_1_j,
       r_ctrl_1_k, ram_ctrl_1_ld, ram_ctrl_1_str, S, sc_ctrl_1_clr, tr_ctrl_1_ld;
  wire [0:0] T;
  wire [2:0] n3bit_fa_1_s, register_1_q;
  wire [6:0] ac_ctrl_1_and, CLEAR_T;
  wire [7:0] D;
  wire [15:0] alu_1_alu_out, bus_1_out_11, ram_1_data;

  not not_1 (not_1_out, HLT);
  SC_CTRL sc_ctrl_1 (.R(R), .I(out_6[15]), .T(CLEAR_T), .D(D), .CLR(sc_ctrl_1_clr));
  and and_1 (and_1_out, 1'b0, HLT);
  or or_1 (or_1_out, and_1_out, and_2_out);
  and and_2 (and_2_out, not_1_out, S);
  Clock clock_1 (.out(clock_1_out));
  and and_3 (CLK, clock_1_out, S);
  Register #(.width(3)) register_1 (.D(n3bit_fa_1_s), .en(S), .Q(register_1_q), .clk(CLK), .clr(or_2_out));
  or or_2 (or_2_out, sc_ctrl_1_clr, and_4_out);
  D_Flip_Flop d_ff_1 (.clk(clock_1_out), .D(or_1_out), .Q(S));  // open: Qn, preset, en, reset
  _3bit_FA u_3bit_fa_1 (.B(register_1_q), .A(3'b001), .S(n3bit_fa_1_s));  // open: COUT
  and and_4 (and_4_out, register_1_q[0], register_1_q[1], register_1_q[2]);
  AC_CTRL ac_ctrl_1 (
    .R(R), .I(out_6[15]), .T({CLEAR_T[5:0], T[0]}), .D(D), .IR(out_6), .AND(ac_ctrl_1_and[0]),
    .ADD(ac_ctrl_1_and[1]), .DR(ac_ctrl_1_and[2]), .INPR(ac_ctrl_1_and[3]), .COM(ac_ctrl_1_and[4]),
    .SHR(ac_ctrl_1_and[5]), .SHL(ac_ctrl_1_and[6]), .INC(ac_ctrl_1_inc), .CLR(ac_ctrl_1_clr));
  Decoder #(.select(3)) decoder_1 (
    .out0(D[0]), .out1(D[1]), .out2(D[2]), .out3(D[3]), .out4(D[4]), .out5(D[5]), .out6(D[6]), .out7(D[7]),
    .sel(out_6[14:12]));  // open: en
  Decoder #(.select(3)) decoder_2 (
    .out0(T[0]), .out1(CLEAR_T[0]), .out2(CLEAR_T[1]), .out3(CLEAR_T[2]), .out4(CLEAR_T[3]),
    .out5(CLEAR_T[4]), .out6(CLEAR_T[5]), .out7(CLEAR_T[6]), .sel(register_1_q));  // open: en
  and and_5 (HLT, D[7], CLEAR_T[2], ~out_6[15], out_6[0]);  // AND_Gate
  ALU alu_1 (.E(out_9), .OPR(ac_ctrl_1_and), .DR(out_4), .AC(out_5), .INPR(INP), .ALU_OUT(alu_1_alu_out), .E_2(ALU_E));
  IR_CTRL ir_ctrl_1 (.R(R), .T({CLEAR_T[5:0], T[0]}), .LD(ir_ctrl_1_ld));
  AR_CTRL ar_ctrl_1 (
    .I(out_6[15]), .D(D), .T({CLEAR_T[5:0], T[0]}), .R(R), .LD(ar_ctrl_1_ld), .INR(ar_ctrl_1_inr),
    .CLR(ar_ctrl_1_clr));
  PC_CTRL pc_ctrl_1 (
    .R(R), .D(D), .T({CLEAR_T[5:0], T[0]}), .IR(out_6), .I(out_6[15]), .DR(out_4), .AC(out_5), .E(out_9),
    .FGI(FGI), .FGO(FGO), .INR(pc_ctrl_1_inr), .LD(pc_ctrl_1_ld), .CLR(pc_ctrl_1_clr));
  DR_CTRL dr_ctrl_1 (.T({CLEAR_T[5:0], T[0]}), .D(D), .LD(dr_ctrl_1_ld), .INR(dr_ctrl_1_inr));
  or or_3 (or_3_out, ac_ctrl_1_and[0], ac_ctrl_1_and[1], ac_ctrl_1_and[2], ac_ctrl_1_and[3], ac_ctrl_1_and[4], ac_ctrl_1_and[5], ac_ctrl_1_and[6]);
  TR_CTRL tr_ctrl_1 (.R(R), .T({CLEAR_T[5:0], T[0]}), .LD(tr_ctrl_1_ld));
  OUTR_CTRL outr_ctrl_1 (.I(out_6[15]), .T({CLEAR_T[5:0], T[0]}), .D(D), .LD(outr_ctrl_1_ld), .IR(out_6));
  R_CTRL r_ctrl_1 (.FGI(FGI), .FGO(FGO), .IEN(IEN), .R(R), .T({CLEAR_T[5:0], T[0]}), .J(r_ctrl_1_j), .K(r_ctrl_1_k));
  RAM_CTRL ram_ctrl_1 (.R(R), .I(out_6[15]), .T({CLEAR_T[5:0], T[0]}), .D(D), .STR(ram_ctrl_1_str), .LD(ram_ctrl_1_ld));
  FGI_CTRL fgi_ctrl_1 (
    .I(out_6[15]), .T({CLEAR_T[5:0], T[0]}), .D(D), .K(fgi_ctrl_1_k), .IR(out_6), .INP(INP), .J(fgi_ctrl_1_j));
  RAM #(.addrWidth(12), .dataWidth(16), .bus("separate")) ram_1 (
    .addr(out_2[11:0]), .din(bus_1_out_11), .data(ram_1_data), .str(ram_ctrl_1_str), .clk(CLK),
    .ld(ram_ctrl_1_ld));  // open: sel, clr
  J_K_Flip_Flop j_k_ff_1 (.J(r_ctrl_1_j), .clk(CLK), .K(r_ctrl_1_k), .Q(R));  // open: Qn, preset, en, reset
  J_K_Flip_Flop j_k_ff_2 (.J(fgi_ctrl_1_j), .clk(CLK), .K(fgi_ctrl_1_k), .Q(FGI));  // open: Qn, preset, en, reset
  AR ar_1 (.CLK(CLK), .CLR(ar_ctrl_1_clr), .LD(ar_ctrl_1_ld), .BUS(bus_1_out_11), .INR(ar_ctrl_1_inr), .AR_OUT(out_2));
  PC pc_1 (.BUS(bus_1_out_11), .PC_OUT(out_3), .INR(pc_ctrl_1_inr), .LD(pc_ctrl_1_ld), .CLK(CLK), .CLR(pc_ctrl_1_clr));
  DR dr_1 (.BUS(bus_1_out_11), .DR_OUT(out_4), .INR(dr_ctrl_1_inr), .LD(dr_ctrl_1_ld), .CLK(CLK));  // open: CLR
  AC ac_1 (.ALU(alu_1_alu_out), .AC_OUT(out_5), .INR(ac_ctrl_1_inc), .LD(or_3_out), .CLK(CLK), .CLR(ac_ctrl_1_clr));
  IR ir_1 (.BUS(bus_1_out_11), .IR_OUT(out_6), .LD(ir_ctrl_1_ld), .CLK(CLK));
  TR tr_1 (.BUS(bus_1_out_11), .DR_OUT(out_7), .INR(1'b0), .LD(tr_ctrl_1_ld), .CLK(CLK));  // open: CLR
  OUTR outr_1 (.LD(outr_ctrl_1_ld), .BUS(bus_1_out_11), .CLK(CLK), .out_4(out_8));
  BUS_CTRL bus_ctrl_1 (
    .R(R), .I(out_6[15]), .T({CLEAR_T[5:0], T[0]}), .D(D), .IR(out_6), .S0(bus_ctrl_1_s0),
    .S1(bus_ctrl_1_s1), .S2(bus_ctrl_1_s2));
  IEN_CTRL ien_ctrl_1 (
    .R(R), .I(out_6[15]), .T({CLEAR_T[5:0], T[0]}), .D(D), .IR(out_6), .K(ien_ctrl_1_k), .J(ien_ctrl_1_j));
  E_CTRL e_ctrl_1 (
    .ALU_E(ALU_E), .I(out_6[15]), .T({CLEAR_T[5:0], T[0]}), .EN(e_ctrl_1_en), .D(D), .J(e_ctrl_1_j),
    .K(e_ctrl_1_k), .IR(out_6), .CLR(e_ctrl_1_clr));
  FGO_CTRL fgo_ctrl_1 (.I(out_6[15]), .T({CLEAR_T[5:0], T[0]}), .D(D), .IR(out_6), .K(fgo_ctrl_1_k), .J(fgo_ctrl_1_j));
  J_K_Flip_Flop j_k_ff_3 (.J(fgo_ctrl_1_j), .clk(CLK), .K(fgo_ctrl_1_k), .Q(FGO));  // open: Qn, preset, en, reset
  BUS bus_1 (
    .S0(bus_ctrl_1_s0), .S1(bus_ctrl_1_s1), .S2(bus_ctrl_1_s2), .AR(out_2), .PC(out_3), .DR(out_4),
    .AC(out_5), .IR(out_6), .TR(out_7), .Mem(ram_1_data), .out_11(bus_1_out_11));
  J_K_Flip_Flop j_k_ff_4 (.J(ien_ctrl_1_j), .clk(CLK), .K(ien_ctrl_1_k), .Q(IEN));  // open: Qn, preset, en, reset
  J_K_Flip_Flop j_k_ff_5 (
    .J(e_ctrl_1_j), .clk(CLK), .K(e_ctrl_1_k), .Q(out_9), .en(e_ctrl_1_en), .reset(e_ctrl_1_clr));  // open: Qn, preset

  // Other names for the same wires on the sheet: IR[15:0] = out_6; AC[15:0] = out_5; T[6:1] = CLEAR_T[5:0];
  //   DR[15:0] = out_4; E = out_9; I = out_6[15]; IR_ADR[11:0] = out_6[11:0]
endmodule

module BUS_CTRL (
  input  R,
  input  I,
  input  [6:0] T,
  input  [7:0] D,
  input  [15:0] IR,
  output S0,
  output S1,
  output S2
);

  wire and_1_out, and_2_out, and_3_out, and_5_out, and_6_out, and_7_out, and_8_out, and_9_out, and_10_out,
       and_11_out, and_12_out, X1, X2, X3, X4, X5, X6, X7;

  Priority_Encoder priority_encoder_1 (
    .in1(X1), .in2(X2), .in3(X3), .in4(X4), .in5(X5), .in6(X6), .in7(X7), .out({S2, S1, S0}));  // open: in0, en_in, gs, en_out
  and and_1 (and_1_out, D[4], T[4]);
  and and_2 (and_2_out, D[5], T[5]);
  and and_3 (and_3_out, D[5], T[4]);
  and and_4 (X3, D[6], T[6]);
  and and_5 (and_5_out, D[7], I, IR[10], T[3]);
  and and_6 (and_6_out, D[3], T[4]);
  and and_7 (and_7_out, ~R, T[1]);  // AND_Gate
  and and_8 (and_8_out, D[0], T[4]);
  and and_9 (and_9_out, D[1], T[4]);
  and and_10 (and_10_out, D[2], T[4]);
  and and_11 (and_11_out, D[6], T[4]);
  and and_12 (and_12_out, I, ~D[7], T[3]);  // AND_Gate
  and and_13 (X5, ~R, T[2]);  // AND_Gate
  and and_14 (X6, R, T[1]);
  or or_1 (X1, and_1_out, and_2_out);
  or or_2 (X2, and_3_out, T[0]);
  or or_3 (X4, and_5_out, and_6_out);
  or or_4 (X7, and_7_out, and_8_out, and_9_out, and_10_out, and_11_out, and_12_out);
endmodule

module BUS (
  input  S0,
  input  S1,
  input  S2,
  input  [15:0] AR,
  input  [15:0] PC,
  input  [15:0] DR,
  input  [15:0] AC,
  input  [15:0] IR,
  input  [15:0] TR,
  input  [15:0] Mem,
  output [15:0] out_11
);

  wire undriven, undriven_2;

  Multiplexer #(.select(3)) multiplexer_1 (
    .in1(AR[0]), .in2(PC[0]), .in3(DR[0]), .in4(AC[0]), .in5(IR[0]), .in6(TR[0]), .in7(Mem[0]),
    .out(out_11[0]), .sel({S2, S1, S0}));  // open: in0, en
  Multiplexer #(.select(3)) multiplexer_2 (
    .in1(AR[1]), .in2(PC[1]), .in3(DR[1]), .in4(AC[1]), .in5(IR[1]), .in6(TR[1]), .in7(Mem[1]),
    .out(out_11[1]), .sel({S2, S1, S0}));  // open: in0, en
  Multiplexer #(.select(3)) multiplexer_3 (
    .in1(AR[2]), .in2(PC[2]), .in3(DR[2]), .in4(AC[2]), .in5(IR[2]), .in6(TR[2]), .in7(Mem[2]),
    .out(out_11[2]), .sel({S2, S1, S0}));  // open: in0, en
  Multiplexer #(.select(3)) multiplexer_4 (
    .in1(AR[3]), .in2(PC[3]), .in3(DR[3]), .in4(AC[3]), .in5(IR[3]), .in6(TR[3]), .in7(Mem[3]),
    .out(out_11[3]), .sel({S2, S1, S0}));  // open: in0, en
  Multiplexer #(.select(3)) multiplexer_5 (
    .in1(AR[4]), .in2(PC[4]), .in3(DR[4]), .in4(AC[4]), .in5(IR[4]), .in6(TR[4]), .in7(Mem[4]),
    .out(out_11[4]), .sel({S2, S1, S0}));  // open: in0, en
  Multiplexer #(.select(3)) multiplexer_6 (
    .in1(AR[5]), .in2(PC[5]), .in3(DR[5]), .in4(AC[5]), .in5(IR[5]), .in6(TR[5]), .in7(Mem[5]),
    .out(out_11[5]), .sel({S2, S1, S0}));  // open: in0, en
  Multiplexer #(.select(3)) multiplexer_7 (
    .in1(AR[6]), .in2(PC[6]), .in3(DR[6]), .in4(AC[6]), .in5(IR[6]), .in6(TR[6]), .in7(Mem[6]),
    .out(out_11[6]), .sel({S2, S1, S0}));  // open: in0, en
  Multiplexer #(.select(3)) multiplexer_8 (
    .in1(AR[7]), .in2(PC[7]), .in3(DR[7]), .in4(AC[7]), .in5(IR[7]), .in6(TR[7]), .in7(Mem[7]),
    .out(out_11[7]), .sel({S2, S1, S0}));  // open: in0, en
  Multiplexer #(.select(3)) multiplexer_9 (
    .in1(AR[8]), .in2(PC[8]), .in3(DR[8]), .in4(AC[8]), .in5(IR[8]), .in6(TR[8]), .in7(Mem[8]),
    .out(out_11[8]), .sel({S2, S1, S0}));  // open: in0, en
  Multiplexer #(.select(3)) multiplexer_10 (
    .in1(AR[9]), .in2(PC[9]), .in3(DR[9]), .in4(AC[9]), .in5(IR[9]), .in6(TR[9]), .in7(Mem[9]),
    .out(out_11[9]), .sel({S2, S1, S0}));  // open: in0, en
  Multiplexer #(.select(3)) multiplexer_11 (
    .in1(AR[10]), .in2(PC[10]), .in3(DR[10]), .in4(AC[10]), .in5(IR[10]), .in6(TR[10]), .in7(Mem[10]),
    .out(out_11[10]), .sel({S2, S1, S0}));  // open: in0, en
  Multiplexer #(.select(3)) multiplexer_12 (
    .in1(AR[11]), .in2(PC[11]), .in3(DR[11]), .in4(AC[11]), .in5(IR[11]), .in6(TR[11]), .in7(Mem[11]),
    .out(out_11[11]), .sel({S2, S1, S0}));  // open: in0, en
  Multiplexer #(.select(3)) multiplexer_13 (
    .in0(undriven_2), .in1(1'b0), .in2(1'b0), .in3(DR[12]), .in4(AC[12]), .in5(IR[12]), .in6(TR[12]),
    .in7(Mem[12]), .out(out_11[12]), .sel({S2, S1, S0}));  // open: en
  Multiplexer #(.select(3)) multiplexer_14 (
    .in0(undriven), .in1(1'b0), .in2(1'b0), .in3(DR[13]), .in4(AC[13]), .in5(IR[13]), .in6(TR[13]),
    .in7(Mem[13]), .out(out_11[13]), .sel({S2, S1, S0}));  // open: en
  Multiplexer #(.select(3)) multiplexer_15 (
    .in1(1'b0), .in2(1'b0), .in3(DR[14]), .in4(AC[14]), .in5(IR[14]), .in6(TR[14]), .in7(Mem[14]),
    .out(out_11[14]), .sel({S2, S1, S0}));  // open: in0, en
  Multiplexer #(.select(3)) multiplexer_16 (
    .in1(1'b0), .in2(1'b0), .in3(DR[15]), .in4(AC[15]), .in5(IR[15]), .in6(TR[15]), .in7(Mem[15]),
    .out(out_11[15]), .sel({S2, S1, S0}));  // open: in0, en

  // Other names for the same wires on the sheet: M0 = Mem[0]; M1 = Mem[1]; M2 = Mem[2]; M3 = Mem[3]; M4 = Mem[4];
  //   M5 = Mem[5]; M6 = Mem[6]; M7 = Mem[7]; M8 = Mem[8]; M9 = Mem[9]; M10 = Mem[10]; M11 = Mem[11]; M12 = Mem[12];
  //   M13 = Mem[13]; M14 = Mem[14]; M15 = Mem[15]
endmodule

module RAM_CTRL (
  input  R,
  input  I,
  input  [6:0] T,
  input  [7:0] D,
  output STR,
  output LD
);

  wire and_1_out, and_2_out, and_3_out, and_4_out, and_5_out, and_6_out, and_7_out, and_8_out, and_9_out,
       and_10_out;

  and and_1 (and_1_out, R, T[1]);
  and and_2 (and_2_out, D[3], T[4]);
  and and_3 (and_3_out, D[5], T[4]);
  and and_4 (and_4_out, D[6], T[6]);
  and and_5 (and_5_out, ~R, T[1]);  // AND_Gate
  and and_6 (and_6_out, D[0], T[4]);
  and and_7 (and_7_out, D[1], T[4]);
  and and_8 (and_8_out, D[2], T[4]);
  and and_9 (and_9_out, D[6], T[4]);
  and and_10 (and_10_out, I, ~D[7], T[3]);  // AND_Gate
  or or_1 (STR, and_1_out, and_2_out, and_3_out, and_4_out);
  or or_2 (LD, and_5_out, and_6_out, and_7_out, and_8_out, and_9_out, and_10_out);
endmodule

module AR_CTRL (
  input  I,
  input  [7:0] D,
  input  [6:0] T,
  input  R,
  output LD,
  output INR,
  output CLR
);

  wire and_1_out, and_2_out, and_3_out, not_1_out, not_2_out;

  not not_1 (not_1_out, D[7]);
  not not_2 (not_2_out, R);
  and and_1 (and_1_out, I, T[3], not_1_out);
  and and_2 (and_2_out, T[2], not_2_out);
  and and_3 (and_3_out, not_2_out, T[0]);
  and and_4 (INR, T[4], D[5]);
  and and_5 (CLR, R, T[0]);
  or or_1 (LD, and_1_out, and_2_out, and_3_out);
endmodule

module AR (
  input  [15:0] BUS,
  input  INR,
  input  LD,
  input  CLK,
  input  CLR,
  output [15:0] AR_OUT
);

  wire or_1_out;
  wire [11:0] multiplexer_1_out, n12bit_fa_1_s;

  or or_1 (or_1_out, INR, LD);
  Multiplexer #(.width(12)) multiplexer_1 (
    .in0(BUS[11:0]), .in1(n12bit_fa_1_s), .out(multiplexer_1_out), .sel(INR));  // open: en
  Register #(.width(12)) register_1 (.D(multiplexer_1_out), .en(or_1_out), .Q(AR_OUT[11:0]), .clk(CLK), .clr(CLR));
  _12bit_FA u_12bit_fa_1 (.B(AR_OUT[11:0]), .A(12'h1), .S(n12bit_fa_1_s));  // open: COUT

  assign AR_OUT[15:12] = 4'b0000;
endmodule

module PC_CTRL (
  input  R,
  input  E,
  input  FGI,
  input  FGO,
  input  I,
  input  [6:0] T,
  input  [7:0] D,
  input  [15:0] IR,
  input  [15:0] DR,
  input  [15:0] AC,
  output LD,
  output CLR,
  output INR
);

  wire AC_prime, and_1_out, and_2_out, and_4_out, and_5_out, and_6_out, and_7_out, and_8_out, and_9_out,
       and_10_out, and_11_out, and_12_out, DR_prime;

  and and_1 (and_1_out, T[4], D[4]);
  and and_2 (and_2_out, T[5], D[5]);
  nor nor_1 (DR_prime, DR[0], DR[1], DR[2], DR[3], DR[4], DR[5], DR[6], DR[7], DR[8], DR[9], DR[10], DR[11], DR[12], DR[13], DR[14], DR[15]);
  nor nor_2 (AC_prime, AC[0], AC[1], AC[2], AC[3], AC[4], AC[5], AC[6], AC[7], AC[8], AC[9], AC[10], AC[11], AC[12], AC[13], AC[14], AC[15]);
  or or_1 (LD, and_1_out, and_2_out);
  and and_3 (CLR, R, T[1]);
  and and_4 (and_4_out, ~R, T[1]);  // AND_Gate
  and and_5 (and_5_out, R, T[2]);
  and and_6 (and_6_out, D[6], T[6], DR_prime);
  and and_7 (and_7_out, ~I, IR[1], T[3], ~E, D[7]);  // AND_Gate
  and and_8 (and_8_out, ~I, IR[2], T[3], AC_prime, D[7]);  // AND_Gate
  and and_9 (and_9_out, ~I, IR[3], AC[15], T[3], D[7]);  // AND_Gate
  and and_10 (and_10_out, ~I, IR[4], ~AC[15], T[3], D[7]);  // AND_Gate
  and and_11 (and_11_out, I, IR[8], T[3], FGO, D[7]);
  and and_12 (and_12_out, I, IR[9], T[3], FGI, D[7]);
  or or_2 (INR, and_4_out, and_5_out, and_6_out, and_7_out, and_8_out, and_9_out, and_10_out, and_11_out, and_12_out);
endmodule

module PC (
  input  [15:0] BUS,
  input  INR,
  input  LD,
  input  CLK,
  input  CLR,
  output [15:0] PC_OUT
);

  wire or_1_out;
  wire [11:0] multiplexer_1_out, n12bit_fa_1_s;

  or or_1 (or_1_out, INR, LD);
  Multiplexer #(.width(12)) multiplexer_1 (
    .in0(BUS[11:0]), .in1(n12bit_fa_1_s), .out(multiplexer_1_out), .sel(INR));  // open: en
  Register #(.width(12)) register_1 (.D(multiplexer_1_out), .en(or_1_out), .Q(PC_OUT[11:0]), .clk(CLK), .clr(CLR));
  _12bit_FA u_12bit_fa_1 (.B(PC_OUT[11:0]), .A(12'h1), .S(n12bit_fa_1_s));  // open: COUT

  assign PC_OUT[15:12] = 4'b0000;
endmodule

module DR_CTRL (
  input  [6:0] T,
  input  [7:0] D,
  output LD,
  output INR
);

  wire and_1_out, and_2_out, and_3_out, and_4_out;

  and and_1 (and_1_out, D[0], T[4]);
  and and_2 (and_2_out, D[1], T[4]);
  and and_3 (and_3_out, D[2], T[4]);
  and and_4 (and_4_out, D[6], T[4]);
  and and_5 (INR, D[6], T[5]);
  or or_1 (LD, and_1_out, and_2_out, and_3_out, and_4_out);
endmodule

module DR (
  input  [15:0] BUS,
  input  INR,
  input  LD,
  input  CLK,
  input  CLR,
  output [15:0] DR_OUT
);

  wire or_1_out;
  wire [15:0] multiplexer_1_out, n16bit_fa_1_s;

  or or_1 (or_1_out, INR, LD);
  Multiplexer #(.width(16)) multiplexer_1 (
    .in0(BUS), .in1(n16bit_fa_1_s), .out(multiplexer_1_out), .sel(INR));  // open: en
  Register #(.width(16)) register_1 (.D(multiplexer_1_out), .en(or_1_out), .Q(DR_OUT), .clk(CLK), .clr(CLR));
  _16bit_FA u_16bit_fa_1 (.B(DR_OUT), .A(16'h1), .S(n16bit_fa_1_s));  // open: COUT
endmodule

module AC_CTRL (
  input  R,
  input  I,
  input  [6:0] T,
  input  [7:0] D,
  input  [15:0] IR,
  output AND,
  output ADD,
  output DR,
  output INPR,
  output COM,
  output SHR,
  output SHL,
  output INC,
  output CLR
);

  wire P, r_t;

  and and_1 (P, D[7], I, T[3]);
  and and_2 (r_t, D[7], ~I, T[3]);  // AND_Gate
  and and_3 (AND, D[0], T[5]);
  and and_4 (ADD, D[1], T[5]);
  and and_5 (DR, D[2], T[5]);
  and and_6 (INPR, P, IR[11]);
  and and_7 (COM, r_t, IR[9]);
  and and_8 (SHR, r_t, IR[7]);
  and and_9 (SHL, IR[6], r_t);
  and and_10 (INC, IR[5], r_t);
  and and_11 (CLR, IR[11], r_t);
endmodule

module AC (
  input  [15:0] ALU,
  input  INR,
  input  LD,
  input  CLK,
  input  CLR,
  output [15:0] AC_OUT
);

  wire or_1_out;
  wire [15:0] multiplexer_1_out, n16bit_fa_1_s;

  or or_1 (or_1_out, INR, LD);
  Multiplexer #(.width(16)) multiplexer_1 (
    .in0(ALU), .in1(n16bit_fa_1_s), .out(multiplexer_1_out), .sel(INR));  // open: en
  Register #(.width(16)) register_1 (.D(multiplexer_1_out), .en(or_1_out), .Q(AC_OUT), .clk(CLK), .clr(CLR));
  _16bit_FA u_16bit_fa_1 (.B(AC_OUT), .A(16'h1), .S(n16bit_fa_1_s));  // open: COUT
endmodule

module ALU (
  input  E,
  input  [6:0] OPR,
  input  [15:0] DR,
  input  [15:0] AC,
  input  [7:0] INPR,
  output [15:0] ALU_OUT,
  output E_2
);

  wire and_1_out, and_2_out, and_3_out, and_4_out, and_5_out, and_6_out, and_7_out, and_8_out, and_9_out,
       and_10_out, and_11_out, and_12_out, and_13_out, and_14_out, and_15_out, and_16_out, and_17_out,
       and_18_out, and_19_out, and_20_out, and_21_out, and_22_out, and_23_out, and_24_out, and_25_out,
       and_26_out, and_27_out, and_28_out, and_29_out, and_30_out, and_31_out, and_32_out, and_33_out,
       and_34_out, and_35_out, and_36_out, and_37_out, and_38_out, and_39_out, and_40_out, and_41_out,
       and_42_out, and_43_out, and_44_out, and_45_out, and_46_out, and_47_out, and_48_out, and_49_out,
       and_50_out, and_51_out, and_52_out, and_53_out, and_54_out, and_55_out, and_56_out, and_57_out,
       and_58_out, and_59_out, and_60_out, and_61_out, and_62_out, and_63_out, and_64_out, and_65_out,
       and_66_out, and_67_out, and_68_out, and_69_out, and_70_out, and_71_out, and_72_out, and_73_out,
       and_74_out, and_75_out, and_76_out, and_77_out, and_78_out, and_79_out, and_80_out, and_81_out,
       and_82_out, and_83_out, and_84_out, and_85_out, and_86_out, and_87_out, and_88_out, and_89_out,
       and_90_out, and_91_out, and_92_out, and_93_out, and_94_out, and_95_out, and_96_out, and_97_out,
       and_98_out, and_99_out, and_100_out, and_101_out, and_102_out, and_103_out, and_104_out, and_105_out,
       and_106_out, and_107_out, and_108_out, and_109_out, and_110_out, and_111_out, and_112_out,
       and_129_out, and_130_out, and_131_out, C1, C2, C3, C4, C5, C6, C7, C8, C9, C10, C11, C12, C13, C14,
       C15, C16, fa_1_s, fa_2_s, fa_3_s, fa_4_s, fa_5_s, fa_6_s, fa_7_s, fa_8_s, fa_9_s, fa_10_s, fa_11_s,
       fa_12_s, fa_13_s, fa_14_s, fa_15_s, fa_16_s, LD, or_2_out, or_3_out, or_4_out, or_5_out, or_6_out,
       or_7_out, or_8_out, or_9_out, or_10_out, or_11_out, or_12_out, or_13_out, or_14_out, or_15_out,
       or_16_out, or_17_out;

  or or_1 (LD, OPR[6], OPR[5], OPR[4], OPR[3], OPR[2], OPR[1], OPR[0]);
  FA fa_1 (.A(AC[0]), .B(DR[0]), .Ci(1'b0), .S(fa_1_s), .Ci_1(C1));
  FA fa_2 (.A(AC[1]), .B(DR[1]), .Ci(C1), .S(fa_2_s), .Ci_1(C2));
  FA fa_3 (.A(AC[2]), .B(DR[2]), .Ci(C2), .S(fa_3_s), .Ci_1(C3));
  FA fa_4 (.A(AC[3]), .B(DR[3]), .Ci(C3), .S(fa_4_s), .Ci_1(C4));
  FA fa_5 (.A(AC[4]), .B(DR[4]), .Ci(C4), .S(fa_5_s), .Ci_1(C5));
  FA fa_6 (.A(AC[5]), .B(DR[5]), .Ci(C5), .S(fa_6_s), .Ci_1(C6));
  FA fa_7 (.A(AC[6]), .B(DR[6]), .Ci(C6), .S(fa_7_s), .Ci_1(C7));
  FA fa_8 (.A(AC[7]), .B(DR[7]), .Ci(C7), .S(fa_8_s), .Ci_1(C8));
  FA fa_9 (.A(AC[8]), .B(DR[8]), .Ci(C8), .S(fa_9_s), .Ci_1(C9));
  FA fa_10 (.A(AC[9]), .B(DR[9]), .Ci(C9), .S(fa_10_s), .Ci_1(C10));
  FA fa_11 (.A(AC[10]), .B(DR[10]), .Ci(C10), .S(fa_11_s), .Ci_1(C11));
  FA fa_12 (.A(AC[11]), .B(DR[11]), .Ci(C11), .S(fa_12_s), .Ci_1(C12));
  FA fa_13 (.A(AC[12]), .B(DR[12]), .Ci(C12), .S(fa_13_s), .Ci_1(C13));
  FA fa_14 (.A(AC[13]), .B(DR[13]), .Ci(C13), .S(fa_14_s), .Ci_1(C14));
  FA fa_15 (.A(AC[14]), .B(DR[14]), .Ci(C14), .S(fa_15_s), .Ci_1(C15));
  FA fa_16 (.A(AC[15]), .B(DR[15]), .Ci(C15), .S(fa_16_s), .Ci_1(C16));
  and and_1 (and_1_out, OPR[0], AC[0], DR[0]);
  and and_2 (and_2_out, OPR[1], fa_1_s);
  and and_3 (and_3_out, OPR[2], DR[0]);
  and and_4 (and_4_out, OPR[3], INPR[0]);
  and and_5 (and_5_out, OPR[4], ~AC[0]);  // AND_Gate
  and and_6 (and_6_out, OPR[5], AC[1]);
  and and_7 (and_7_out, OPR[6], E);
  and and_8 (and_8_out, OPR[0], AC[1], DR[1]);
  and and_9 (and_9_out, OPR[1], fa_2_s);
  and and_10 (and_10_out, OPR[2], DR[1]);
  and and_11 (and_11_out, OPR[3], INPR[1]);
  and and_12 (and_12_out, OPR[4], ~AC[1]);  // AND_Gate
  and and_13 (and_13_out, OPR[5], AC[2]);
  and and_14 (and_14_out, OPR[6], AC[0]);
  and and_15 (and_15_out, OPR[0], AC[2], DR[2]);
  and and_16 (and_16_out, OPR[1], fa_3_s);
  and and_17 (and_17_out, OPR[2], DR[2]);
  and and_18 (and_18_out, OPR[3], INPR[2]);
  and and_19 (and_19_out, OPR[4], ~AC[2]);  // AND_Gate
  and and_20 (and_20_out, OPR[5], AC[3]);
  and and_21 (and_21_out, OPR[6], AC[1]);
  and and_22 (and_22_out, OPR[0], AC[3], DR[3]);
  and and_23 (and_23_out, OPR[1], fa_4_s);
  and and_24 (and_24_out, OPR[2], DR[3]);
  and and_25 (and_25_out, OPR[3], INPR[3]);
  and and_26 (and_26_out, OPR[4], ~AC[3]);  // AND_Gate
  and and_27 (and_27_out, OPR[5], AC[4]);
  and and_28 (and_28_out, OPR[6], AC[2]);
  and and_29 (and_29_out, OPR[0], AC[4], DR[4]);
  and and_30 (and_30_out, OPR[1], fa_5_s);
  and and_31 (and_31_out, OPR[2], DR[4]);
  and and_32 (and_32_out, OPR[3], INPR[4]);
  and and_33 (and_33_out, OPR[4], ~AC[4]);  // AND_Gate
  and and_34 (and_34_out, OPR[5], AC[5]);
  and and_35 (and_35_out, OPR[6], AC[3]);
  and and_36 (and_36_out, OPR[0], AC[5], DR[5]);
  and and_37 (and_37_out, OPR[1], fa_6_s);
  and and_38 (and_38_out, OPR[2], DR[5]);
  and and_39 (and_39_out, OPR[3], INPR[5]);
  and and_40 (and_40_out, OPR[4], ~AC[5]);  // AND_Gate
  and and_41 (and_41_out, OPR[5], AC[6]);
  and and_42 (and_42_out, OPR[6], AC[4]);
  and and_43 (and_43_out, OPR[0], AC[6], DR[6]);
  and and_44 (and_44_out, OPR[1], fa_7_s);
  and and_45 (and_45_out, OPR[2], DR[6]);
  and and_46 (and_46_out, OPR[3], INPR[6]);
  and and_47 (and_47_out, OPR[4], ~AC[6]);  // AND_Gate
  and and_48 (and_48_out, OPR[5], AC[7]);
  and and_49 (and_49_out, OPR[6], AC[5]);
  and and_50 (and_50_out, OPR[0], AC[7], DR[7]);
  and and_51 (and_51_out, OPR[1], fa_8_s);
  and and_52 (and_52_out, OPR[2], DR[7]);
  and and_53 (and_53_out, OPR[3], INPR[7]);
  and and_54 (and_54_out, OPR[4], ~AC[7]);  // AND_Gate
  and and_55 (and_55_out, OPR[5], AC[8]);
  and and_56 (and_56_out, OPR[6], AC[6]);
  and and_57 (and_57_out, OPR[0], AC[8], DR[8]);
  and and_58 (and_58_out, OPR[1], fa_9_s);
  and and_59 (and_59_out, OPR[2], DR[8]);
  and and_60 (and_60_out, OPR[3], 1'b0);
  and and_61 (and_61_out, OPR[4], ~AC[8]);  // AND_Gate
  and and_62 (and_62_out, OPR[5], AC[9]);
  and and_63 (and_63_out, OPR[6], AC[7]);
  and and_64 (and_64_out, OPR[0], AC[9], DR[9]);
  and and_65 (and_65_out, OPR[1], fa_10_s);
  and and_66 (and_66_out, OPR[2], DR[9]);
  and and_67 (and_67_out, OPR[3], 1'b0);
  and and_68 (and_68_out, OPR[4], ~AC[9]);  // AND_Gate
  and and_69 (and_69_out, OPR[5], AC[10]);
  and and_70 (and_70_out, OPR[6], AC[8]);
  and and_71 (and_71_out, OPR[0], AC[10], DR[10]);
  and and_72 (and_72_out, OPR[1], fa_11_s);
  and and_73 (and_73_out, OPR[2], DR[10]);
  and and_74 (and_74_out, OPR[3], 1'b0);
  and and_75 (and_75_out, OPR[4], ~AC[10]);  // AND_Gate
  and and_76 (and_76_out, OPR[5], AC[11]);
  and and_77 (and_77_out, OPR[6], AC[9]);
  and and_78 (and_78_out, OPR[0], AC[11], DR[11]);
  and and_79 (and_79_out, OPR[1], fa_12_s);
  and and_80 (and_80_out, OPR[2], DR[11]);
  and and_81 (and_81_out, OPR[3], 1'b0);
  and and_82 (and_82_out, OPR[4], ~AC[11]);  // AND_Gate
  and and_83 (and_83_out, OPR[5], AC[12]);
  and and_84 (and_84_out, OPR[6], AC[10]);
  and and_85 (and_85_out, OPR[0], AC[12], DR[12]);
  and and_86 (and_86_out, OPR[1], fa_13_s);
  and and_87 (and_87_out, OPR[2], DR[12]);
  and and_88 (and_88_out, OPR[3], 1'b0);
  and and_89 (and_89_out, OPR[4], ~AC[12]);  // AND_Gate
  and and_90 (and_90_out, OPR[5], AC[13]);
  and and_91 (and_91_out, OPR[6], AC[11]);
  and and_92 (and_92_out, OPR[0], AC[13], DR[13]);
  and and_93 (and_93_out, OPR[1], fa_14_s);
  and and_94 (and_94_out, OPR[2], DR[13]);
  and and_95 (and_95_out, OPR[3], 1'b0);
  and and_96 (and_96_out, OPR[4], ~AC[13]);  // AND_Gate
  and and_97 (and_97_out, OPR[5], AC[14]);
  and and_98 (and_98_out, OPR[6], AC[12]);
  and and_99 (and_99_out, OPR[0], AC[14], DR[14]);
  and and_100 (and_100_out, OPR[1], fa_15_s);
  and and_101 (and_101_out, OPR[2], DR[14]);
  and and_102 (and_102_out, OPR[3], 1'b0);
  and and_103 (and_103_out, OPR[4], ~AC[14]);  // AND_Gate
  and and_104 (and_104_out, OPR[5], AC[15]);
  and and_105 (and_105_out, OPR[6], AC[13]);
  and and_106 (and_106_out, OPR[0], AC[15], DR[15]);
  and and_107 (and_107_out, OPR[1], fa_16_s);
  and and_108 (and_108_out, OPR[2], DR[15]);
  and and_109 (and_109_out, OPR[3], 1'b0);
  and and_110 (and_110_out, OPR[4], ~AC[15]);  // AND_Gate
  and and_111 (and_111_out, OPR[5], E);
  and and_112 (and_112_out, OPR[6], AC[14]);
  or or_2 (or_2_out, and_1_out, and_2_out, and_3_out, and_4_out, and_5_out, and_6_out, and_7_out);
  or or_3 (or_3_out, and_8_out, and_9_out, and_10_out, and_11_out, and_12_out, and_13_out, and_14_out);
  or or_4 (or_4_out, and_15_out, and_16_out, and_17_out, and_18_out, and_19_out, and_20_out, and_21_out);
  or or_5 (or_5_out, and_22_out, and_23_out, and_24_out, and_25_out, and_26_out, and_27_out, and_28_out);
  or or_6 (or_6_out, and_29_out, and_30_out, and_31_out, and_32_out, and_33_out, and_34_out, and_35_out);
  or or_7 (or_7_out, and_36_out, and_37_out, and_38_out, and_39_out, and_40_out, and_41_out, and_42_out);
  or or_8 (or_8_out, and_43_out, and_44_out, and_45_out, and_46_out, and_47_out, and_48_out, and_49_out);
  or or_9 (or_9_out, and_50_out, and_51_out, and_52_out, and_53_out, and_54_out, and_55_out, and_56_out);
  or or_10 (or_10_out, and_57_out, and_58_out, and_59_out, and_60_out, and_61_out, and_62_out, and_63_out);
  or or_11 (or_11_out, and_64_out, and_65_out, and_66_out, and_67_out, and_68_out, and_69_out, and_70_out);
  or or_12 (or_12_out, and_71_out, and_72_out, and_73_out, and_74_out, and_75_out, and_76_out, and_77_out);
  or or_13 (or_13_out, and_78_out, and_79_out, and_80_out, and_81_out, and_82_out, and_83_out, and_84_out);
  or or_14 (or_14_out, and_85_out, and_86_out, and_87_out, and_88_out, and_89_out, and_90_out, and_91_out);
  or or_15 (or_15_out, and_92_out, and_93_out, and_94_out, and_95_out, and_96_out, and_97_out, and_98_out);
  or or_16 (or_16_out, and_99_out, and_100_out, and_101_out, and_102_out, and_103_out, and_104_out, and_105_out);
  or or_17 (or_17_out, and_106_out, and_107_out, and_108_out, and_109_out, and_110_out, and_111_out, and_112_out);
  and and_113 (ALU_OUT[0], LD, or_2_out);
  and and_114 (ALU_OUT[1], LD, or_3_out);
  and and_115 (ALU_OUT[2], LD, or_4_out);
  and and_116 (ALU_OUT[3], LD, or_5_out);
  and and_117 (ALU_OUT[4], LD, or_6_out);
  and and_118 (ALU_OUT[5], LD, or_7_out);
  and and_119 (ALU_OUT[6], LD, or_8_out);
  and and_120 (ALU_OUT[7], LD, or_9_out);
  and and_121 (ALU_OUT[8], LD, or_10_out);
  and and_122 (ALU_OUT[9], LD, or_11_out);
  and and_123 (ALU_OUT[10], LD, or_12_out);
  and and_124 (ALU_OUT[11], LD, or_13_out);
  and and_125 (ALU_OUT[12], LD, or_14_out);
  and and_126 (ALU_OUT[13], LD, or_15_out);
  and and_127 (ALU_OUT[14], LD, or_16_out);
  and and_128 (ALU_OUT[15], LD, or_17_out);
  and and_129 (and_129_out, OPR[1], C16);
  and and_130 (and_130_out, OPR[5], AC[0]);
  and and_131 (and_131_out, OPR[6], AC[15]);
  or or_18 (E_2, and_129_out, and_130_out, and_131_out);

  // Other names for the same wires on the sheet: I0 = ALU_OUT[0]; I1 = ALU_OUT[1]; I2 = ALU_OUT[2]; I3 = ALU_OUT[3];
  //   I4 = ALU_OUT[4]; I5 = ALU_OUT[5]; I6 = ALU_OUT[6]; I7 = ALU_OUT[7]; I8 = ALU_OUT[8]; I9 = ALU_OUT[9];
  //   I10 = ALU_OUT[10]; I11 = ALU_OUT[11]; I12 = ALU_OUT[12]; I13 = ALU_OUT[13]; I14 = ALU_OUT[14];
  //   I15 = ALU_OUT[15]; INP0 = INPR[0]; INP1 = INPR[1]; INP2 = INPR[2]; INP3 = INPR[3]; INP4 = INPR[4];
  //   INP5 = INPR[5]; INP6 = INPR[6]; INP7 = INPR[7]; AND = OPR[0]; ADD = OPR[1]; DR_t = OPR[2]; INPR_t = OPR[3];
  //   COM = OPR[4]; SHR = OPR[5]; SHL = OPR[6]
endmodule

module IR_CTRL (
  input  R,
  input  [6:0] T,
  output LD
);

  and and_1 (LD, ~R, T[1]);  // AND_Gate
endmodule

module IR (
  input  [15:0] BUS,
  input  LD,
  input  CLK,
  output [15:0] IR_OUT
);

  Register #(.width(16)) register_1 (.D(BUS), .en(LD), .Q(IR_OUT), .clk(CLK));  // open: clr
endmodule

module TR_CTRL (
  input  R,
  input  [6:0] T,
  output LD
);

  and and_1 (LD, R, T[0]);
endmodule

module TR (
  input  [15:0] BUS,
  input  INR,
  input  LD,
  input  CLK,
  input  CLR,
  output [15:0] DR_OUT
);

  wire or_1_out;
  wire [15:0] multiplexer_1_out, n16bit_fa_1_s;

  or or_1 (or_1_out, INR, LD);
  Multiplexer #(.width(16)) multiplexer_1 (
    .in0(BUS), .in1(n16bit_fa_1_s), .out(multiplexer_1_out), .sel(INR));  // open: en
  Register #(.width(16)) register_1 (.D(multiplexer_1_out), .en(or_1_out), .Q(DR_OUT), .clk(CLK), .clr(CLR));
  _16bit_FA u_16bit_fa_1 (.B(DR_OUT), .A(16'h1), .S(n16bit_fa_1_s));  // open: COUT
endmodule

module OUTR_CTRL (
  input  I,
  input  [6:0] T,
  input  [7:0] D,
  input  [15:0] IR,
  output LD
);

  and and_1 (LD, I, T[3], D[7], IR[10]);
endmodule

module OUTR (
  input  LD,
  input  [15:0] BUS,
  input  CLK,
  output [7:0] out_4
);

  Counter counter_1 (.load(LD), .D(BUS[7:0]), .count(1'b0), .Q(out_4), .clk(CLK), .clr(1'b0));  // open: carry
endmodule

module SC_CTRL (
  input  R,
  input  I,
  input  [6:0] T,
  input  [7:0] D,
  output CLR
);

  wire and_1_out, and_2_out, and_3_out, and_4_out, and_5_out, and_6_out, and_7_out, and_8_out, and_9_out,
       and_10_out;

  and and_1 (and_1_out, R, T[2]);
  and and_2 (and_2_out, D[0], T[5]);
  and and_3 (and_3_out, D[1], T[5]);
  and and_4 (and_4_out, D[2], T[5]);
  and and_5 (and_5_out, D[3], T[4]);
  and and_6 (and_6_out, D[4], T[4]);
  and and_7 (and_7_out, D[5], T[5]);
  and and_8 (and_8_out, D[6], T[6]);
  and and_9 (and_9_out, D[7], T[3], I);
  and and_10 (and_10_out, D[7], T[3], ~I);  // AND_Gate
  or or_1 (CLR, and_1_out, and_2_out, and_3_out, and_4_out, and_5_out, and_6_out, and_7_out, and_8_out, and_9_out, and_10_out);
endmodule

module S_CTRL (
  input  I,
  input  [6:0] T,
  input  [7:0] D,
  input  [15:0] IR,
  output CLR
);

  and and_1 (CLR, ~I, T[3], D[7], IR[0]);  // AND_Gate
endmodule

module FGI_CTRL (
  input  [7:0] INP,
  input  I,
  input  [6:0] T,
  input  [7:0] D,
  input  [15:0] IR,
  output J,
  output K
);

  or or_1 (J, INP[0], INP[1], INP[2], INP[3], INP[4], INP[5], INP[6], INP[7]);
  and and_1 (K, I, T[3], D[7], IR[11]);
endmodule

module FGO_CTRL (
  input  I,
  input  [6:0] T,
  input  [7:0] D,
  input  [15:0] IR,
  output J,
  output K
);

  and and_1 (K, ~I, T[3], D[7], IR[10]);  // AND_Gate

  assign J = D[0];
endmodule

module IEN_CTRL (
  input  R,
  input  I,
  input  [6:0] T,
  input  [7:0] D,
  input  [15:0] IR,
  output K,
  output J
);

  wire and_1_out, and_2_out;

  and and_1 (and_1_out, R, T[2]);
  and and_2 (and_2_out, D[7], I, T[3], IR[6]);
  and and_3 (J, D[7], I, T[3], IR[7]);
  or or_1 (K, and_1_out, and_2_out);
endmodule

module R_CTRL (
  input  FGI,
  input  FGO,
  input  IEN,
  input  R,
  input  [6:0] T,
  output J,
  output K
);

  wire or_1_out;

  or or_1 (or_1_out, FGI, FGO);
  and and_1 (J, or_1_out, IEN, ~T[0], ~T[1], ~T[2]);  // AND_Gate
  and and_2 (K, R, T[2]);
endmodule

module E_CTRL (
  input  ALU_E,
  input  I,
  input  [6:0] T,
  input  [7:0] D,
  input  [15:0] IR,
  output EN,
  output J,
  output K,
  output CLR
);

  wire and_1_out, and_2_out, and_3_out, or_1_out;

  or or_1 (or_1_out, IR[6], IR[7]);
  and and_1 (and_1_out, D[1], T[5]);
  and and_2 (and_2_out, D[7], ~I, T[3], or_1_out);  // AND_Gate
  and and_3 (and_3_out, D[7], ~I, T[3], IR[8]);  // AND_Gate
  and and_4 (CLR, D[7], ~I, T[3], IR[10]);  // AND_Gate
  or or_2 (EN, and_1_out, and_2_out);
  Multiplexer multiplexer_1 (.in0(ALU_E), .in1(and_3_out), .out(J), .sel(and_3_out));  // open: en
  and and_5 (K, J, and_3_out);
endmodule

module FA (
  input  A,
  input  B,
  input  Ci,
  output S,
  output Ci_1
);

  wire and_1_out, and_2_out, xor_1_out;

  xor xor_1 (xor_1_out, A, B);
  and and_1 (and_1_out, A, B);
  xor xor_2 (S, xor_1_out, Ci);
  and and_2 (and_2_out, xor_1_out, Ci);
  or or_1 (Ci_1, and_2_out, and_1_out);
endmodule

module _3bit_FA (
  input  [2:0] A,
  input  [2:0] B,
  output COUT,
  output [2:0] S
);

  wire fa_1_ci_1, fa_2_ci_1, fa_3_ci_1;

  FA fa_1 (.A(A[2]), .B(B[2]), .Ci(fa_2_ci_1), .S(S[2]), .Ci_1(fa_1_ci_1));
  FA fa_2 (.A(A[1]), .B(B[1]), .Ci(fa_3_ci_1), .S(S[1]), .Ci_1(fa_2_ci_1));
  FA fa_3 (.A(A[0]), .B(B[0]), .Ci(1'b0), .S(S[0]), .Ci_1(fa_3_ci_1));
endmodule

module _4bit_FA (
  input  [3:0] A,
  input  [3:0] B,
  output COUT,
  output [3:0] S
);

  wire fa_1_ci_1, fa_2_ci_1, fa_3_ci_1, fa_4_ci_1;

  FA fa_1 (.A(A[3]), .B(B[3]), .Ci(fa_2_ci_1), .S(S[3]), .Ci_1(fa_1_ci_1));
  FA fa_2 (.A(A[2]), .B(B[2]), .Ci(fa_3_ci_1), .S(S[2]), .Ci_1(fa_2_ci_1));
  FA fa_3 (.A(A[1]), .B(B[1]), .Ci(fa_4_ci_1), .S(S[1]), .Ci_1(fa_3_ci_1));
  FA fa_4 (.A(A[0]), .B(B[0]), .Ci(1'b0), .S(S[0]), .Ci_1(fa_4_ci_1));
endmodule

module _12bit_FA (
  input  [11:0] A,
  input  [11:0] B,
  output COUT,
  output [11:0] S
);

  wire fa_1_ci_1, fa_2_ci_1, fa_3_ci_1, fa_4_ci_1, fa_5_ci_1, fa_6_ci_1, fa_7_ci_1, fa_8_ci_1, fa_9_ci_1,
       fa_10_ci_1, fa_11_ci_1, fa_12_ci_1;

  FA fa_1 (.A(A[11]), .B(B[11]), .Ci(fa_2_ci_1), .S(S[11]), .Ci_1(fa_1_ci_1));
  FA fa_2 (.A(A[10]), .B(B[10]), .Ci(fa_3_ci_1), .S(S[10]), .Ci_1(fa_2_ci_1));
  FA fa_3 (.A(A[9]), .B(B[9]), .Ci(fa_4_ci_1), .S(S[9]), .Ci_1(fa_3_ci_1));
  FA fa_4 (.A(A[8]), .B(B[8]), .Ci(fa_5_ci_1), .S(S[8]), .Ci_1(fa_4_ci_1));
  FA fa_5 (.A(A[7]), .B(B[7]), .Ci(fa_6_ci_1), .S(S[7]), .Ci_1(fa_5_ci_1));
  FA fa_6 (.A(A[6]), .B(B[6]), .Ci(fa_7_ci_1), .S(S[6]), .Ci_1(fa_6_ci_1));
  FA fa_7 (.A(A[5]), .B(B[5]), .Ci(fa_8_ci_1), .S(S[5]), .Ci_1(fa_7_ci_1));
  FA fa_8 (.A(A[4]), .B(B[4]), .Ci(fa_9_ci_1), .S(S[4]), .Ci_1(fa_8_ci_1));
  FA fa_9 (.A(A[3]), .B(B[3]), .Ci(fa_10_ci_1), .S(S[3]), .Ci_1(fa_9_ci_1));
  FA fa_10 (.A(A[2]), .B(B[2]), .Ci(fa_11_ci_1), .S(S[2]), .Ci_1(fa_10_ci_1));
  FA fa_11 (.A(A[1]), .B(B[1]), .Ci(fa_12_ci_1), .S(S[1]), .Ci_1(fa_11_ci_1));
  FA fa_12 (.A(A[0]), .B(B[0]), .Ci(1'b0), .S(S[0]), .Ci_1(fa_12_ci_1));
endmodule

module _16bit_FA (
  input  [15:0] A,
  input  [15:0] B,
  output COUT,
  output [15:0] S
);

  wire fa_1_ci_1, fa_2_ci_1, fa_3_ci_1, fa_4_ci_1, fa_5_ci_1, fa_6_ci_1, fa_7_ci_1, fa_8_ci_1, fa_9_ci_1,
       fa_10_ci_1, fa_11_ci_1, fa_12_ci_1, fa_13_ci_1, fa_14_ci_1, fa_15_ci_1, fa_16_ci_1;

  FA fa_1 (.A(B[15]), .B(A[15]), .Ci(fa_2_ci_1), .S(S[15]), .Ci_1(fa_1_ci_1));
  FA fa_2 (.A(B[14]), .B(A[14]), .Ci(fa_3_ci_1), .S(S[14]), .Ci_1(fa_2_ci_1));
  FA fa_3 (.A(B[13]), .B(A[13]), .Ci(fa_4_ci_1), .S(S[13]), .Ci_1(fa_3_ci_1));
  FA fa_4 (.A(B[12]), .B(A[12]), .Ci(fa_5_ci_1), .S(S[12]), .Ci_1(fa_4_ci_1));
  FA fa_5 (.A(A[11]), .B(B[11]), .Ci(fa_6_ci_1), .S(S[11]), .Ci_1(fa_5_ci_1));
  FA fa_6 (.A(A[10]), .B(B[10]), .Ci(fa_7_ci_1), .S(S[10]), .Ci_1(fa_6_ci_1));
  FA fa_7 (.A(A[9]), .B(B[9]), .Ci(fa_8_ci_1), .S(S[9]), .Ci_1(fa_7_ci_1));
  FA fa_8 (.A(A[8]), .B(B[8]), .Ci(fa_9_ci_1), .S(S[8]), .Ci_1(fa_8_ci_1));
  FA fa_9 (.A(A[7]), .B(B[7]), .Ci(fa_10_ci_1), .S(S[7]), .Ci_1(fa_9_ci_1));
  FA fa_10 (.A(A[6]), .B(B[6]), .Ci(fa_11_ci_1), .S(S[6]), .Ci_1(fa_10_ci_1));
  FA fa_11 (.A(A[5]), .B(B[5]), .Ci(fa_12_ci_1), .S(S[5]), .Ci_1(fa_11_ci_1));
  FA fa_12 (.A(A[4]), .B(B[4]), .Ci(fa_13_ci_1), .S(S[4]), .Ci_1(fa_12_ci_1));
  FA fa_13 (.A(A[3]), .B(B[3]), .Ci(fa_14_ci_1), .S(S[3]), .Ci_1(fa_13_ci_1));
  FA fa_14 (.A(A[2]), .B(B[2]), .Ci(fa_15_ci_1), .S(S[2]), .Ci_1(fa_14_ci_1));
  FA fa_15 (.A(A[1]), .B(B[1]), .Ci(fa_16_ci_1), .S(S[1]), .Ci_1(fa_15_ci_1));
  FA fa_16 (.A(A[0]), .B(B[0]), .Ci(1'b0), .S(S[0]), .Ci_1(fa_16_ci_1));
endmodule
